// Logisim project CPU.circ as structural Verilog: 12 circuits, main circuit main
// Load Store Address
module main (
  input  in_1,
  input  in_2,
  output out_3,
  output [17:0] out_4,
  output [3:0] out_5,
  output [9:0] out_6
);

  wire ALU_signal, and_1_out, beq, bge, bgt, ble, blt, Branch_Enable, branch_signal, comparator_18_bit_1_eq,
       comparator_18_bit_1_gt, comparator_18_bit_1_lt, imm_signal, jump_signal, n, not_1_out, not_2_out,
       or_1_out, p, store_signal, SystemClock, xnor_1_out, xnor_2_out, xnor_3_out, z;
  wire [1:0] Operation;
  wire [3:0] multiplexer_2_out, multiplexer_3_out, multiplexer_5_out, Op2, SR2;
  wire [5:0] control_unit_1_out_3, control_unit_1_out_4;
  wire [9:0] control_unit_1_jump_address;
  wire [17:0] ALU_Result, Branch_Address, imm_value, Jump_Address, multiplexer_1_out, multiplexer_4_out,
       multiplexer_6_out, multiplexer_7_out, Op1_Data, Op2_Data, program_counter_1_pc_address, rom_1_data,
       value_in_mem_address;

  // Probe on rom_1_data
  Multiplexer #(.width(18)) multiplexer_1 (
    .in0(Jump_Address), .in1(Branch_Address), .out(multiplexer_1_out), .sel(branch_signal));  // open: en
  Register #(.width(18)) Instruction_Register (.D(rom_1_data), .Q(out_4), .clk(SystemClock), .clr(in_2));  // open: en
  Multiplexer #(.width(4)) multiplexer_2 (
    .in0(Op2), .in1(out_5), .out(multiplexer_2_out), .sel(store_signal));  // open: en
  Comparator_18_bit comparator_18_bit_1 (
    .a(Op1_Data), .b(Op2_Data), .EQ(comparator_18_bit_1_eq), .LT(comparator_18_bit_1_lt),
    .GT(comparator_18_bit_1_gt));
  and and_1 (and_1_out, Branch_Enable, branch_signal);
  Multiplexer #(.width(4)) multiplexer_3 (
    .in0(out_5), .in1(multiplexer_2_out), .out(multiplexer_3_out), .sel(not_1_out));  // open: en
  not not_1 (not_1_out, branch_signal);
  Program_Counter program_counter_1 (
    .ADDR(multiplexer_1_out), .jump_signal(jump_signal), .branch_signal(and_1_out),
    .PC_address(program_counter_1_pc_address), .Clock(SystemClock), .Clear(in_1));
  not not_2 (not_2_out, branch_signal);
  or or_1 (or_1_out, ALU_signal, out_3);
  xnor xnor_1 (xnor_1_out, z, comparator_18_bit_1_eq);
  xnor xnor_2 (xnor_2_out, comparator_18_bit_1_lt, n);
  xnor xnor_3 (xnor_3_out, comparator_18_bit_1_gt, p);
  Multiplexer #(.width(18)) multiplexer_4 (
    .in0(value_in_mem_address), .in1(ALU_Result), .out(multiplexer_4_out), .sel(ALU_signal));  // open: en
  Register_File register_file_1 (
    .Reg_Write(out_5), .Write_Enable(or_1_out), .out_7(Op1_Data), .Clock(SystemClock),
    .in_1(multiplexer_4_out), .read_which_reg2_(multiplexer_5_out), .read_which_reg1(multiplexer_3_out),
    .out_8(Op2_Data));
  Multiplexer #(.width(4)) multiplexer_5 (.in0(Op2), .in1(SR2), .out(multiplexer_5_out), .sel(not_2_out));  // open: en
  and and_2 (Branch_Enable, xnor_1_out, xnor_2_out, xnor_3_out);
  Clock clock_1 (.out(SystemClock));
  ROM #(.addrWidth(18), .dataWidth(18)) rom_1 (.addr(program_counter_1_pc_address), .data(rom_1_data));  // open: sel
  Multiplexer #(.width(18)) multiplexer_6 (
    .in0(Op2_Data), .in1(imm_value), .out(multiplexer_6_out), .sel(imm_signal));  // open: en
  or or_2 (branch_signal, blt, ble, bge, bgt, beq);
  ALU_18_bit alu_18_bit_1 (
    .A(Op1_Data), .B(multiplexer_6_out), .Output(ALU_Result), .ChooseOperation(Operation));  // open: carry_out
  Multiplexer #(.width(18)) multiplexer_7 (
    .in1(Op1_Data), .out(multiplexer_7_out), .sel(store_signal));  // open: in0, en
  Control_Unit control_unit_1 (
    .Instruction(out_4), .Load(out_3), .Load_Store_Adress(out_6), .Dest(out_5), .BGT(bgt), .SR1(Op2),
    .SR2(SR2), .imm_signal(imm_signal), .ALU_signal(ALU_signal), .Operation(Operation),
    .out_4(control_unit_1_out_4), .BEQ(beq), .BLT(blt), .BLE(ble), .BGE(bge), .Store(store_signal),
    .Jump(jump_signal), .out_3(control_unit_1_out_3), .n(n), .z(z), .p(p),
    .Jump_Address(control_unit_1_jump_address));
  Extender_6_18 extender_6_18_1 (.in_1(control_unit_1_out_3), .out_2(Branch_Address));
  RAM #(.addrWidth(10), .dataWidth(18), .bus("separate")) ram_1 (
    .addr(out_6), .din(multiplexer_7_out), .data(value_in_mem_address), .str(store_signal),
    .clk(SystemClock), .ld(out_3));  // open: sel, clr
  Extender_10_18 extender_10_18_1 (.in(control_unit_1_jump_address), .out(Jump_Address));
  Extender_6_18 extender_6_18_2 (.in_1(control_unit_1_out_4), .out_2(imm_value));

  // Other names for the same wires on the sheet: Address[9:0] = out_6; dest_reg[3:0] = out_5; Op1[3:0] = out_5;
  //   Instruction[17:0] = out_4; load_signal = out_3; Reset = in_1; SR1[3:0] = Op2

  // Notes on the sheet:
  //   z
  //   n
  //   p
  //   Program Counter
  //   Instruction Memory
  //   contents of rom_1 (hex, n*v repeats v):
  //   6a8b 7b81 7f40 7780 3b7c 2a688 6641 3c3fb 37c00
  //   Data Memory
endmodule

module ALU_1_bit (
  input  Carry_in,
  input  Ax,
  input  Bx,
  input  [1:0] Operantion,
  output Carry_out,
  output Result
);

  wire ADD, AND, OR, XOR;

  Multiplexer #(.select(2)) multiplexer_1 (
    .in0(ADD), .in1(AND), .in2(OR), .in3(XOR), .out(Result), .sel(Operantion));  // open: en
  and and_1 (AND, Bx, Ax);
  or or_1 (OR, Bx, Ax);
  Adder_1_bit adder_1_bit_1 (.a(Bx), .b(Ax), .ci(Carry_in), .co(Carry_out), .s(ADD));
  xor xor_1 (XOR, Ax, Bx);
endmodule

module ALU_18_bit (
  input  [17:0] A,
  input  [17:0] B,
  input  [1:0] ChooseOperation,
  output [17:0] Output,
  output carry_out
);

  wire alu_1_bit_1_carry_out, alu_1_bit_2_carry_out, alu_1_bit_3_carry_out, alu_1_bit_4_carry_out,
       alu_1_bit_5_carry_out, alu_1_bit_6_carry_out, alu_1_bit_7_carry_out, alu_1_bit_8_carry_out,
       alu_1_bit_9_carry_out, alu_1_bit_10_carry_out, alu_1_bit_11_carry_out, alu_1_bit_12_carry_out,
       alu_1_bit_13_carry_out, alu_1_bit_14_carry_out, alu_1_bit_15_carry_out, alu_1_bit_16_carry_out,
       alu_1_bit_17_carry_out;

  ALU_1_bit alu_1_bit_1 (
    .Ax(A[0]), .Bx(B[0]), .Result(Output[0]), .Carry_in(1'b0), .Operantion(ChooseOperation),
    .Carry_out(alu_1_bit_1_carry_out));
  ALU_1_bit alu_1_bit_2 (
    .Ax(A[1]), .Bx(B[1]), .Result(Output[1]), .Carry_in(alu_1_bit_1_carry_out), .Operantion(ChooseOperation),
    .Carry_out(alu_1_bit_2_carry_out));
  ALU_1_bit alu_1_bit_3 (
    .Ax(A[2]), .Bx(B[2]), .Result(Output[2]), .Carry_in(alu_1_bit_2_carry_out), .Operantion(ChooseOperation),
    .Carry_out(alu_1_bit_3_carry_out));
  ALU_1_bit alu_1_bit_4 (
    .Ax(A[3]), .Bx(B[3]), .Result(Output[3]), .Carry_in(alu_1_bit_3_carry_out), .Operantion(ChooseOperation),
    .Carry_out(alu_1_bit_4_carry_out));
  ALU_1_bit alu_1_bit_5 (
    .Ax(A[4]), .Bx(B[4]), .Result(Output[4]), .Carry_in(alu_1_bit_4_carry_out), .Operantion(ChooseOperation),
    .Carry_out(alu_1_bit_5_carry_out));
  ALU_1_bit alu_1_bit_6 (
    .Ax(A[5]), .Bx(B[5]), .Result(Output[5]), .Carry_in(alu_1_bit_5_carry_out), .Operantion(ChooseOperation),
    .Carry_out(alu_1_bit_6_carry_out));
  ALU_1_bit alu_1_bit_7 (
    .Ax(A[6]), .Bx(B[6]), .Result(Output[6]), .Carry_in(alu_1_bit_6_carry_out), .Operantion(ChooseOperation),
    .Carry_out(alu_1_bit_7_carry_out));
  ALU_1_bit alu_1_bit_8 (
    .Ax(A[7]), .Bx(B[7]), .Result(Output[7]), .Carry_in(alu_1_bit_7_carry_out), .Operantion(ChooseOperation),
    .Carry_out(alu_1_bit_8_carry_out));
  ALU_1_bit alu_1_bit_9 (
    .Ax(A[8]), .Bx(B[8]), .Result(Output[8]), .Carry_in(alu_1_bit_8_carry_out), .Operantion(ChooseOperation),
    .Carry_out(alu_1_bit_9_carry_out));
  ALU_1_bit alu_1_bit_10 (
    .Ax(B[9]), .Bx(A[9]), .Result(Output[9]), .Carry_in(alu_1_bit_9_carry_out), .Operantion(ChooseOperation),
    .Carry_out(alu_1_bit_10_carry_out));
  ALU_1_bit alu_1_bit_11 (
    .Ax(A[10]), .Bx(B[10]), .Result(Output[10]), .Carry_in(alu_1_bit_10_carry_out),
    .Operantion(ChooseOperation), .Carry_out(alu_1_bit_11_carry_out));
  ALU_1_bit alu_1_bit_12 (
    .Ax(A[11]), .Bx(B[11]), .Result(Output[11]), .Carry_in(alu_1_bit_11_carry_out),
    .Operantion(ChooseOperation), .Carry_out(alu_1_bit_12_carry_out));
  ALU_1_bit alu_1_bit_13 (
    .Ax(A[12]), .Bx(B[12]), .Result(Output[12]), .Carry_in(alu_1_bit_12_carry_out),
    .Operantion(ChooseOperation), .Carry_out(alu_1_bit_13_carry_out));
  ALU_1_bit alu_1_bit_14 (
    .Ax(A[13]), .Bx(B[13]), .Result(Output[13]), .Carry_in(alu_1_bit_13_carry_out),
    .Operantion(ChooseOperation), .Carry_out(alu_1_bit_14_carry_out));
  ALU_1_bit alu_1_bit_15 (
    .Ax(A[14]), .Bx(B[14]), .Result(Output[14]), .Carry_in(alu_1_bit_14_carry_out),
    .Operantion(ChooseOperation), .Carry_out(alu_1_bit_15_carry_out));
  ALU_1_bit alu_1_bit_16 (
    .Ax(A[15]), .Bx(B[15]), .Result(Output[15]), .Carry_in(alu_1_bit_15_carry_out),
    .Operantion(ChooseOperation), .Carry_out(alu_1_bit_16_carry_out));
  ALU_1_bit alu_1_bit_17 (
    .Ax(A[16]), .Bx(B[16]), .Result(Output[16]), .Carry_in(alu_1_bit_16_carry_out),
    .Operantion(ChooseOperation), .Carry_out(alu_1_bit_17_carry_out));
  ALU_1_bit alu_1_bit_18 (
    .Ax(A[17]), .Bx(B[17]), .Result(Output[17]), .Carry_in(alu_1_bit_17_carry_out),
    .Operantion(ChooseOperation), .Carry_out(carry_out));
endmodule

module Control_Unit (
  input  [17:0] Instruction,
  output [9:0] Jump_Address,
  output [5:0] out_3,
  output [5:0] out_4,
  output [9:0] Load_Store_Adress,
  output [3:0] SR1,
  output p,
  output z,
  output [3:0] Dest,
  output [3:0] SR2,
  output n,
  output [1:0] Operation,
  output imm_signal,
  output Load,
  output ALU_signal,
  output BGT,
  output Store,
  output BEQ,
  output BGE,
  output BLT,
  output BLE,
  output Jump
);

  not not_1 (ALU_signal, Instruction[17]);
  Decoder #(.select(4)) decoder_1 (
    .out8(Load), .out9(BGT), .out10(BEQ), .out11(BGE), .out12(BLT), .out13(Store), .out14(BLE), .out15(Jump),
    .sel(Instruction[17:14]));  // open: out0, out1, out2, out3, out4, out5, out6, out7, en

  assign Dest = Instruction[13:10];
  assign imm_signal = Instruction[14];
  assign Jump_Address = Instruction[9:0];
  assign Load_Store_Adress = Instruction[9:0];
  assign n = Instruction[16];
  assign Operation = Instruction[16:15];
  assign out_3 = Instruction[5:0];
  assign out_4 = Instruction[5:0];
  assign p = Instruction[14];
  assign SR1 = Instruction[9:6];
  assign SR2 = Instruction[5:2];
  assign z = Instruction[15];

  // Other names for the same wires on the sheet: ADDR[9:0] = Instruction[9:0]; Branch_Address[5:0] = Instruction[5:0];
  //   imm[5:0] = Instruction[5:0]; OpCode[3:0] = Instruction[17:14]; Reg[3:0] = Instruction[13:10]

  // Notes on the sheet:
  //   Opcode Analyzer
  //   Output register
  //   Output adress
  //   ALU
endmodule

module Register_File (
  input  [17:0] in_1,
  input  [3:0] Reg_Write,
  input  [3:0] read_which_reg1,
  input  [3:0] read_which_reg2_,
  input  Write_Enable,
  input  Clock,
  output [17:0] out_7,
  output [17:0] out_8
);

  wire and_1_out, and_2_out, and_3_out, and_4_out, and_5_out, and_6_out, and_7_out, and_8_out, and_9_out,
       and_10_out, and_11_out, and_12_out, and_13_out, and_14_out, and_15_out, and_16_out, decoder_1_out0,
       decoder_1_out1, decoder_1_out2, decoder_1_out3, decoder_1_out4, decoder_1_out5, decoder_1_out6,
       decoder_1_out7, decoder_1_out8, decoder_1_out9, decoder_1_out10, decoder_1_out11, decoder_1_out12,
       decoder_1_out13, decoder_1_out14, decoder_1_out15;
  wire [17:0] R0_q, R1_q, R2_q, R3_q, R4_q, R5_q, R6_q, R7_q, R8_q, R9_q, R10_q, R11_q, R12_q, R13_q, R14_q,
       R15_q;

  Decoder #(.select(4)) decoder_1 (
    .out0(decoder_1_out0), .out1(decoder_1_out1), .out2(decoder_1_out2), .out3(decoder_1_out3),
    .out4(decoder_1_out4), .out5(decoder_1_out5), .out6(decoder_1_out6), .out7(decoder_1_out7),
    .out8(decoder_1_out8), .out9(decoder_1_out9), .out10(decoder_1_out10), .out11(decoder_1_out11),
    .out12(decoder_1_out12), .out13(decoder_1_out13), .out14(decoder_1_out14), .out15(decoder_1_out15),
    .sel(Reg_Write));  // open: en
  and and_1 (and_1_out, decoder_1_out0, Write_Enable);
  and and_2 (and_2_out, decoder_1_out1, Write_Enable);
  and and_3 (and_3_out, decoder_1_out2, Write_Enable);
  and and_4 (and_4_out, decoder_1_out3, Write_Enable);
  and and_5 (and_5_out, decoder_1_out4, Write_Enable);
  and and_6 (and_6_out, decoder_1_out5, Write_Enable);
  and and_7 (and_7_out, decoder_1_out6, Write_Enable);
  and and_8 (and_8_out, decoder_1_out7, Write_Enable);
  and and_9 (and_9_out, decoder_1_out8, Write_Enable);
  and and_10 (and_10_out, decoder_1_out9, Write_Enable);
  and and_11 (and_11_out, decoder_1_out10, Write_Enable);
  and and_12 (and_12_out, decoder_1_out11, Write_Enable);
  and and_13 (and_13_out, decoder_1_out12, Write_Enable);
  and and_14 (and_14_out, decoder_1_out13, Write_Enable);
  and and_15 (and_15_out, decoder_1_out14, Write_Enable);
  and and_16 (and_16_out, decoder_1_out15, Write_Enable);
  Register #(.width(18)) R0 (.D(in_1), .en(and_1_out), .Q(R0_q), .clk(Clock));  // open: clr
  Register #(.width(18)) R1 (.D(in_1), .en(and_2_out), .Q(R1_q), .clk(Clock));  // open: clr
  Register #(.width(18)) R2 (.D(in_1), .en(and_3_out), .Q(R2_q), .clk(Clock));  // open: clr
  Register #(.width(18)) R3 (.D(in_1), .en(and_4_out), .Q(R3_q), .clk(Clock));  // open: clr
  Register #(.width(18)) R4 (.D(in_1), .en(and_5_out), .Q(R4_q), .clk(Clock));  // open: clr
  Register #(.width(18)) R5 (.D(in_1), .en(and_6_out), .Q(R5_q), .clk(Clock));  // open: clr
  Register #(.width(18)) R6 (.D(in_1), .en(and_7_out), .Q(R6_q), .clk(Clock));  // open: clr
  Register #(.width(18)) R7 (.D(in_1), .en(and_8_out), .Q(R7_q), .clk(Clock));  // open: clr
  Register #(.width(18)) R8 (.D(in_1), .en(and_9_out), .Q(R8_q), .clk(Clock));  // open: clr
  Register #(.width(18)) R9 (.D(in_1), .en(and_10_out), .Q(R9_q), .clk(Clock));  // open: clr
  Register #(.width(18)) R10 (.D(in_1), .en(and_11_out), .Q(R10_q), .clk(Clock));  // open: clr
  Register #(.width(18)) R11 (.D(in_1), .en(and_12_out), .Q(R11_q), .clk(Clock));  // open: clr
  Register #(.width(18)) R12 (.D(in_1), .en(and_13_out), .Q(R12_q), .clk(Clock));  // open: clr
  Register #(.width(18)) R13 (.D(in_1), .en(and_14_out), .Q(R13_q), .clk(Clock));  // open: clr
  Register #(.width(18)) R14 (.D(in_1), .en(and_15_out), .Q(R14_q), .clk(Clock));  // open: clr
  Register #(.width(18)) R15 (.D(in_1), .en(and_16_out), .Q(R15_q), .clk(Clock));  // open: clr
  Multiplexer #(.select(4), .width(18)) multiplexer_1 (
    .in0(R0_q), .in1(R1_q), .in2(R2_q), .in3(R3_q), .in4(R4_q), .in5(R5_q), .in6(R6_q), .in7(R7_q),
    .in8(R8_q), .in9(R9_q), .in10(R10_q), .in11(R11_q), .in12(R12_q), .in13(R13_q), .in14(R14_q),
    .in15(R15_q), .out(out_7), .sel(read_which_reg1));  // open: en
  Multiplexer #(.select(4), .width(18)) multiplexer_2 (
    .in0(R0_q), .in1(R1_q), .in2(R2_q), .in3(R3_q), .in4(R4_q), .in5(R5_q), .in6(R6_q), .in7(R7_q),
    .in8(R8_q), .in9(R9_q), .in10(R10_q), .in11(R11_q), .in12(R12_q), .in13(R13_q), .in14(R14_q),
    .in15(R15_q), .out(out_8), .sel(read_which_reg2_));  // open: en

  // Notes on the sheet:
  //   data in
endmodule

module Adder_1_bit (
  input  ci,
  input  a,
  input  b,
  output s,
  output co
);

  wire and_1_out, and_2_out, and_3_out, xor_1_out;

  and and_1 (and_1_out, a, ci);
  and and_2 (and_2_out, a, b);
  or or_1 (co, and_2_out, and_1_out, and_3_out);
  and and_3 (and_3_out, b, ci);
  xor xor_1 (xor_1_out, a, b);
  xor xor_2 (s, xor_1_out, ci);
endmodule

module Adder_18_bit (
  input  [17:0] a,
  input  [17:0] b,
  output [17:0] s,
  output co
);

  wire adder_1_bit_1_co, adder_1_bit_2_co, adder_1_bit_3_co, adder_1_bit_4_co, adder_1_bit_5_co,
       adder_1_bit_6_co, adder_1_bit_7_co, adder_1_bit_8_co, adder_1_bit_9_co, adder_1_bit_10_co,
       adder_1_bit_11_co, adder_1_bit_12_co, adder_1_bit_13_co, adder_1_bit_14_co, adder_1_bit_15_co,
       adder_1_bit_16_co, adder_1_bit_17_co;

  Adder_1_bit adder_1_bit_1 (.a(a[0]), .b(b[0]), .ci(1'b0), .co(adder_1_bit_1_co), .s(s[0]));
  Adder_1_bit adder_1_bit_2 (.a(a[1]), .b(b[1]), .ci(adder_1_bit_1_co), .co(adder_1_bit_2_co), .s(s[1]));
  Adder_1_bit adder_1_bit_3 (.a(a[2]), .b(b[2]), .ci(adder_1_bit_2_co), .co(adder_1_bit_3_co), .s(s[2]));
  Adder_1_bit adder_1_bit_4 (.a(a[3]), .b(b[3]), .ci(adder_1_bit_3_co), .co(adder_1_bit_4_co), .s(s[3]));
  Adder_1_bit adder_1_bit_5 (.a(a[4]), .b(b[4]), .ci(adder_1_bit_4_co), .co(adder_1_bit_5_co), .s(s[4]));
  Adder_1_bit adder_1_bit_6 (.a(a[5]), .b(b[5]), .ci(adder_1_bit_5_co), .co(adder_1_bit_6_co), .s(s[5]));
  Adder_1_bit adder_1_bit_7 (.a(a[6]), .b(b[6]), .ci(adder_1_bit_6_co), .co(adder_1_bit_7_co), .s(s[6]));
  Adder_1_bit adder_1_bit_8 (.a(a[7]), .b(b[7]), .ci(adder_1_bit_7_co), .co(adder_1_bit_8_co), .s(s[7]));
  Adder_1_bit adder_1_bit_9 (.a(a[8]), .b(b[8]), .ci(adder_1_bit_8_co), .co(adder_1_bit_9_co), .s(s[8]));
  Adder_1_bit adder_1_bit_10 (.a(a[9]), .b(b[9]), .ci(adder_1_bit_9_co), .co(adder_1_bit_10_co), .s(s[9]));
  Adder_1_bit adder_1_bit_11 (.a(a[10]), .b(b[10]), .ci(adder_1_bit_10_co), .co(adder_1_bit_11_co), .s(s[10]));
  Adder_1_bit adder_1_bit_12 (.a(a[11]), .b(b[11]), .ci(adder_1_bit_11_co), .co(adder_1_bit_12_co), .s(s[11]));
  Adder_1_bit adder_1_bit_13 (.a(a[12]), .b(b[12]), .ci(adder_1_bit_12_co), .co(adder_1_bit_13_co), .s(s[12]));
  Adder_1_bit adder_1_bit_14 (.a(a[13]), .b(b[13]), .ci(adder_1_bit_13_co), .co(adder_1_bit_14_co), .s(s[13]));
  Adder_1_bit adder_1_bit_15 (.a(a[14]), .b(b[14]), .ci(adder_1_bit_14_co), .co(adder_1_bit_15_co), .s(s[14]));
  Adder_1_bit adder_1_bit_16 (.a(a[15]), .b(b[15]), .ci(adder_1_bit_15_co), .co(adder_1_bit_16_co), .s(s[15]));
  Adder_1_bit adder_1_bit_17 (.a(a[16]), .b(b[16]), .ci(adder_1_bit_16_co), .co(adder_1_bit_17_co), .s(s[16]));
  Adder_1_bit adder_1_bit_18 (.a(a[17]), .b(b[17]), .ci(adder_1_bit_17_co), .co(co), .s(s[17]));
endmodule

module Comparator_1_bit (
  input  a,
  input  b,
  output GT,
  output EQ,
  output LT
);

  wire not_1_out;

  xnor xnor_1 (EQ, a, b);
  not not_1 (not_1_out, EQ);
  and and_1 (GT, a, not_1_out);
  and and_2 (LT, b, not_1_out);

  // Notes on the sheet:
  //   if not eq
endmodule

module Comparator_18_bit (
  input  [17:0] a,
  input  [17:0] b,
  output EQ,
  output LT,
  output GT
);

  wire and_1_out, and_2_out, and_3_out, and_4_out, and_5_out, and_6_out, and_7_out, and_8_out, and_9_out,
       and_10_out, and_11_out, and_12_out, and_13_out, and_14_out, and_15_out, and_16_out, and_17_out,
       comparator_1_bit_1_eq, comparator_1_bit_1_gt, comparator_1_bit_2_eq, comparator_1_bit_2_gt,
       comparator_1_bit_3_eq, comparator_1_bit_3_gt, comparator_1_bit_4_eq, comparator_1_bit_4_gt,
       comparator_1_bit_5_eq, comparator_1_bit_5_gt, comparator_1_bit_6_eq, comparator_1_bit_6_gt,
       comparator_1_bit_7_eq, comparator_1_bit_7_gt, comparator_1_bit_8_eq, comparator_1_bit_8_gt,
       comparator_1_bit_9_eq, comparator_1_bit_9_gt, comparator_1_bit_10_eq, comparator_1_bit_10_gt,
       comparator_1_bit_11_eq, comparator_1_bit_11_gt, comparator_1_bit_12_eq, comparator_1_bit_12_gt,
       comparator_1_bit_13_eq, comparator_1_bit_13_gt, comparator_1_bit_14_eq, comparator_1_bit_14_gt,
       comparator_1_bit_15_eq, comparator_1_bit_15_gt, comparator_1_bit_16_eq, comparator_1_bit_16_gt,
       comparator_1_bit_17_eq, comparator_1_bit_17_gt, comparator_1_bit_18_eq, comparator_1_bit_18_gt;

  Comparator_1_bit comparator_1_bit_1 (
    .GT(comparator_1_bit_1_gt), .EQ(comparator_1_bit_1_eq), .a(a[0]), .b(b[0]));  // open: LT
  Comparator_1_bit comparator_1_bit_2 (
    .GT(comparator_1_bit_2_gt), .EQ(comparator_1_bit_2_eq), .a(a[1]), .b(b[1]));  // open: LT
  Comparator_1_bit comparator_1_bit_3 (
    .GT(comparator_1_bit_3_gt), .EQ(comparator_1_bit_3_eq), .a(a[2]), .b(b[2]));  // open: LT
  Comparator_1_bit comparator_1_bit_4 (
    .GT(comparator_1_bit_4_gt), .EQ(comparator_1_bit_4_eq), .a(a[3]), .b(b[3]));  // open: LT
  Comparator_1_bit comparator_1_bit_5 (
    .GT(comparator_1_bit_5_gt), .EQ(comparator_1_bit_5_eq), .a(a[4]), .b(b[4]));  // open: LT
  Comparator_1_bit comparator_1_bit_6 (
    .GT(comparator_1_bit_6_gt), .EQ(comparator_1_bit_6_eq), .a(a[5]), .b(b[5]));  // open: LT
  Comparator_1_bit comparator_1_bit_7 (
    .GT(comparator_1_bit_7_gt), .EQ(comparator_1_bit_7_eq), .a(a[6]), .b(b[6]));  // open: LT
  Comparator_1_bit comparator_1_bit_8 (
    .GT(comparator_1_bit_8_gt), .EQ(comparator_1_bit_8_eq), .a(a[7]), .b(b[7]));  // open: LT
  Comparator_1_bit comparator_1_bit_9 (
    .GT(comparator_1_bit_9_gt), .EQ(comparator_1_bit_9_eq), .a(a[8]), .b(b[8]));  // open: LT
  Comparator_1_bit comparator_1_bit_10 (
    .GT(comparator_1_bit_10_gt), .EQ(comparator_1_bit_10_eq), .a(a[9]), .b(b[9]));  // open: LT
  Comparator_1_bit comparator_1_bit_11 (
    .GT(comparator_1_bit_11_gt), .EQ(comparator_1_bit_11_eq), .a(a[10]), .b(b[10]));  // open: LT
  Comparator_1_bit comparator_1_bit_12 (
    .GT(comparator_1_bit_12_gt), .EQ(comparator_1_bit_12_eq), .a(a[11]), .b(b[11]));  // open: LT
  Comparator_1_bit comparator_1_bit_13 (
    .GT(comparator_1_bit_13_gt), .EQ(comparator_1_bit_13_eq), .a(a[12]), .b(b[12]));  // open: LT
  Comparator_1_bit comparator_1_bit_14 (
    .GT(comparator_1_bit_14_gt), .EQ(comparator_1_bit_14_eq), .a(a[13]), .b(b[13]));  // open: LT
  Comparator_1_bit comparator_1_bit_15 (
    .GT(comparator_1_bit_15_gt), .EQ(comparator_1_bit_15_eq), .a(a[14]), .b(b[14]));  // open: LT
  Comparator_1_bit comparator_1_bit_16 (
    .GT(comparator_1_bit_16_gt), .EQ(comparator_1_bit_16_eq), .a(a[15]), .b(b[15]));  // open: LT
  Comparator_1_bit comparator_1_bit_17 (
    .GT(comparator_1_bit_17_gt), .EQ(comparator_1_bit_17_eq), .a(a[16]), .b(b[16]));  // open: LT
  Comparator_1_bit comparator_1_bit_18 (
    .GT(comparator_1_bit_18_gt), .EQ(comparator_1_bit_18_eq), .a(a[17]), .b(b[17]));  // open: LT
  and and_1 (and_1_out, comparator_1_bit_1_gt, comparator_1_bit_2_eq, comparator_1_bit_3_eq, comparator_1_bit_4_eq, comparator_1_bit_5_eq, comparator_1_bit_6_eq, comparator_1_bit_7_eq, comparator_1_bit_8_eq, comparator_1_bit_9_eq, comparator_1_bit_10_eq, comparator_1_bit_11_eq, comparator_1_bit_12_eq, comparator_1_bit_13_eq, comparator_1_bit_14_eq, comparator_1_bit_15_eq, comparator_1_bit_16_eq, comparator_1_bit_17_eq, comparator_1_bit_18_eq);
  and and_2 (and_2_out, comparator_1_bit_2_gt, comparator_1_bit_3_eq, comparator_1_bit_4_eq, comparator_1_bit_5_eq, comparator_1_bit_6_eq, comparator_1_bit_7_eq, comparator_1_bit_8_eq, comparator_1_bit_9_eq, comparator_1_bit_10_eq, comparator_1_bit_11_eq, comparator_1_bit_12_eq, comparator_1_bit_13_eq, comparator_1_bit_14_eq, comparator_1_bit_15_eq, comparator_1_bit_16_eq, comparator_1_bit_17_eq, comparator_1_bit_18_eq);
  and and_3 (and_3_out, comparator_1_bit_3_gt, comparator_1_bit_4_eq, comparator_1_bit_5_eq, comparator_1_bit_6_eq, comparator_1_bit_7_eq, comparator_1_bit_8_eq, comparator_1_bit_9_eq, comparator_1_bit_10_eq, comparator_1_bit_11_eq, comparator_1_bit_12_eq, comparator_1_bit_13_eq, comparator_1_bit_14_eq, comparator_1_bit_15_eq, comparator_1_bit_16_eq, comparator_1_bit_17_eq, comparator_1_bit_18_eq);
  and and_4 (and_4_out, comparator_1_bit_4_gt, comparator_1_bit_5_eq, comparator_1_bit_6_eq, comparator_1_bit_7_eq, comparator_1_bit_8_eq, comparator_1_bit_9_eq, comparator_1_bit_10_eq, comparator_1_bit_11_eq, comparator_1_bit_12_eq, comparator_1_bit_13_eq, comparator_1_bit_14_eq, comparator_1_bit_15_eq, comparator_1_bit_16_eq, comparator_1_bit_17_eq, comparator_1_bit_18_eq);
  and and_5 (and_5_out, comparator_1_bit_5_gt, comparator_1_bit_6_eq, comparator_1_bit_7_eq, comparator_1_bit_8_eq, comparator_1_bit_9_eq, comparator_1_bit_10_eq, comparator_1_bit_11_eq, comparator_1_bit_12_eq, comparator_1_bit_13_eq, comparator_1_bit_14_eq, comparator_1_bit_15_eq, comparator_1_bit_16_eq, comparator_1_bit_17_eq, comparator_1_bit_18_eq);
  and and_6 (and_6_out, comparator_1_bit_6_gt, comparator_1_bit_7_eq, comparator_1_bit_8_eq, comparator_1_bit_9_eq, comparator_1_bit_10_eq, comparator_1_bit_11_eq, comparator_1_bit_12_eq, comparator_1_bit_13_eq, comparator_1_bit_14_eq, comparator_1_bit_15_eq, comparator_1_bit_16_eq, comparator_1_bit_17_eq, comparator_1_bit_18_eq);
  and and_7 (and_7_out, comparator_1_bit_7_gt, comparator_1_bit_8_eq, comparator_1_bit_9_eq, comparator_1_bit_10_eq, comparator_1_bit_11_eq, comparator_1_bit_12_eq, comparator_1_bit_13_eq, comparator_1_bit_14_eq, comparator_1_bit_15_eq, comparator_1_bit_16_eq, comparator_1_bit_17_eq, comparator_1_bit_18_eq);
  and and_8 (and_8_out, comparator_1_bit_8_gt, comparator_1_bit_9_eq, comparator_1_bit_10_eq, comparator_1_bit_11_eq, comparator_1_bit_12_eq, comparator_1_bit_13_eq, comparator_1_bit_14_eq, comparator_1_bit_15_eq, comparator_1_bit_16_eq, comparator_1_bit_17_eq, comparator_1_bit_18_eq);
  and and_9 (and_9_out, comparator_1_bit_9_gt, comparator_1_bit_10_eq, comparator_1_bit_11_eq, comparator_1_bit_12_eq, comparator_1_bit_13_eq, comparator_1_bit_14_eq, comparator_1_bit_15_eq, comparator_1_bit_16_eq, comparator_1_bit_17_eq, comparator_1_bit_18_eq);
  and and_10 (and_10_out, comparator_1_bit_10_gt, comparator_1_bit_11_eq, comparator_1_bit_12_eq, comparator_1_bit_13_eq, comparator_1_bit_14_eq, comparator_1_bit_15_eq, comparator_1_bit_16_eq, comparator_1_bit_17_eq, comparator_1_bit_18_eq);
  and and_11 (and_11_out, comparator_1_bit_11_gt, comparator_1_bit_12_eq, comparator_1_bit_13_eq, comparator_1_bit_14_eq, comparator_1_bit_15_eq, comparator_1_bit_16_eq, comparator_1_bit_17_eq, comparator_1_bit_18_eq);
  and and_12 (and_12_out, comparator_1_bit_12_gt, comparator_1_bit_13_eq, comparator_1_bit_14_eq, comparator_1_bit_15_eq, comparator_1_bit_16_eq, comparator_1_bit_17_eq, comparator_1_bit_18_eq);
  and and_13 (and_13_out, comparator_1_bit_13_gt, comparator_1_bit_13_eq, comparator_1_bit_14_eq, comparator_1_bit_15_eq, comparator_1_bit_17_eq, comparator_1_bit_18_eq);
  and and_14 (and_14_out, comparator_1_bit_14_gt, comparator_1_bit_15_eq, comparator_1_bit_16_eq, comparator_1_bit_17_eq, comparator_1_bit_18_eq);
  and and_15 (and_15_out, comparator_1_bit_15_gt, comparator_1_bit_16_eq, comparator_1_bit_17_eq, comparator_1_bit_18_eq);
  and and_16 (and_16_out, comparator_1_bit_16_gt, comparator_1_bit_17_eq, comparator_1_bit_18_eq);
  and and_17 (and_17_out, comparator_1_bit_17_gt, comparator_1_bit_18_eq);
  and and_18 (EQ, comparator_1_bit_1_eq, comparator_1_bit_2_eq, comparator_1_bit_3_eq, comparator_1_bit_4_eq, comparator_1_bit_5_eq, comparator_1_bit_6_eq, comparator_1_bit_7_eq, comparator_1_bit_8_eq, comparator_1_bit_9_eq, comparator_1_bit_10_eq, comparator_1_bit_11_eq, comparator_1_bit_12_eq, comparator_1_bit_13_eq, comparator_1_bit_14_eq, comparator_1_bit_15_eq, comparator_1_bit_16_eq, comparator_1_bit_17_eq, comparator_1_bit_18_eq);
  nor nor_1 (LT, EQ, GT);
  or or_1 (GT, and_1_out, and_2_out, and_3_out, and_4_out, and_5_out, and_6_out, and_7_out, and_8_out, and_9_out, and_10_out, and_11_out, and_12_out, and_13_out, and_14_out, and_15_out, and_16_out, and_17_out, comparator_1_bit_18_gt);
endmodule

module Extender_6_18 (
  input  [5:0] in_1,
  output [17:0] out_2
);

  Multiplexer #(.width(12)) multiplexer_1 (
    .in0({12{1'b0}}), .in1({12{1'b1}}), .out(out_2[17:6]), .sel(in_1[5]));  // open: en

  assign out_2[5:0] = in_1;

  // Other names for the same wires on the sheet: isNegative = in_1[5]
endmodule

module Extender_10_18 (
  input  [9:0] in,
  output [17:0] out
);

  Multiplexer #(.width(8)) multiplexer_1 (.in0({8{1'b0}}), .in1({8{1'b1}}), .out(out[17:10]), .sel(in[9]));  // open: en

  assign out[9:0] = in;

  // Other names for the same wires on the sheet: isNegative = in[9]
endmodule

module Program_Counter (
  input  [17:0] ADDR,
  input  jump_signal,
  input  Clear,
  input  Clock,
  input  branch_signal,
  output [17:0] PC_address
);

  wire [17:0] adder_18_bit_1_s, multiplexer_1_out, multiplexer_2_out, multiplexer_3_out;

  Multiplexer #(.width(18)) multiplexer_1 (
    .in0(18'h1), .in1(ADDR), .out(multiplexer_1_out), .sel(jump_signal));  // open: en
  Adder_18_bit adder_18_bit_1 (.a(multiplexer_1_out), .b(PC_address), .s(adder_18_bit_1_s));  // open: co
  Multiplexer #(.width(18)) multiplexer_2 (
    .in0(adder_18_bit_1_s), .in1(multiplexer_3_out), .out(multiplexer_2_out), .sel(branch_signal));  // open: en
  Register #(.width(18), .trigger("falling")) register_1 (
    .D(multiplexer_2_out), .Q(PC_address), .clk(Clock), .clr(Clear));  // open: en
  Multiplexer #(.width(18)) multiplexer_3 (.in1(ADDR), .out(multiplexer_3_out), .sel(branch_signal));  // open: in0, en
endmodule
